// Logisim project I012_Lab01_25520317.circ as structural Verilog: 6 circuits, main circuit THINGHIEM1
module THINGHIEM0 (
  input  A,
  input  B,
  output F
);

  wire not_1_out;

  not not_1 (not_1_out, B);
  and and_1 (F, A, not_1_out);
endmodule

module THINGHIEM1 (
  input  A,
  input  B,
  input  C,
  output NOT,
  output AND,
  output OR,
  output NAND,
  output NOR,
  output XOR,
  output XNOR,
  output XOR3,
  output NAND3,
  output CHAIN
);

  not not_1 (NOT, A);
  and and_1 (AND, A, B);
  or or_1 (OR, A, B);
  nand nand_1 (NAND, A, B);
  nor nor_1 (NOR, A, B);
  xor xor_1 (XOR, B, B);
  xnor xnor_1 (XNOR, A, B);
  ExactlyOne xor_2 (.out(XOR3), .in0(A), .in1(B), .in2(C));
  nand nand_2 (NAND3, A, B, C);
  nand nand_3 (CHAIN, NAND, C);
endmodule

module THINGHIEM2 (
  input  x,
  input  y,
  input  z,
  output EQ1,
  output EQ2,
  output EQ3,
  output EQ4,
  output EQ5
);

  wire not_1_out, not_2_out, x_prime_y_out, x_prime_y_prime_out, x_x_prime_y_out, x_y___x_z_out,
       x_y__prime_2_out, x_y__prime_out, x_y_out, x_y_z_out, x_z_out, y_z_out;

  not not_1 (not_1_out, x);
  not not_2 (not_2_out, y);
  and y_z (y_z_out, y, z);
  nor x_y__prime (x_y__prime_out, x, y);
  nand x_y__prime_2 (x_y__prime_2_out, x, y);
  or x_y_z (x_y_z_out, x, y_z_out);
  or x_y (x_y_out, x, y);
  or x_z (x_z_out, x, z);
  and x_prime_y (x_prime_y_out, not_1_out, y);
  and x_prime_y_prime (x_prime_y_prime_out, not_1_out, not_2_out);
  and x_y___x_z (x_y___x_z_out, x_y_out, x_z_out);
  or x_x_prime_y (x_x_prime_y_out, x_prime_y_out, x);
  xnor xnor_1 (EQ1, x_y__prime_out, x_prime_y_prime_out);
  xnor xnor_2 (EQ2, x_prime_y_prime_out, x_y__prime_2_out);
  xnor xnor_3 (EQ3, x_y_z_out, x_y___x_z_out);
  xnor xnor_4 (EQ4, x, x_x_prime_y_out);
  xnor xnor_5 (EQ5, x_y_out, x_x_prime_y_out);
endmodule

module THINGHIEM3 (
  input  A,
  input  B,
  input  C,
  input  D,
  output F
);

  wire m2_out, m3_out, m5_out, m7_out, m11_out, m13_out, not_1_out, not_2_out, not_3_out, not_4_out;

  not not_1 (not_1_out, A);
  not not_2 (not_2_out, B);
  not not_3 (not_3_out, C);
  not not_4 (not_4_out, D);
  and m2 (m2_out, not_1_out, not_2_out, C, not_4_out);
  and m3 (m3_out, not_1_out, not_2_out, C, D);
  and m5 (m5_out, not_1_out, B, not_3_out, D);
  and m7 (m7_out, not_1_out, B, C, D);
  and m11 (m11_out, A, not_2_out, C, D);
  and m13 (m13_out, A, B, not_3_out, D);
  or SoP (F, m2_out, m3_out, m5_out, m7_out, m11_out, m13_out);
endmodule

module THINGHIEM4 (
  input  A,
  input  B,
  input  C,
  input  D,
  output F_can,
  output EQ1,
  output EQ2,
  output F_sop,
  output F_pos
);

  wire A_prime_B_prime_C_out, A_prime_B_prime_C_prime_out, A_prime_BD_out, A_prime_D_out, B_C_out,
       B_prime_CD_out, B_prime_D_out, BC_prime_D_out, C_D_out, m2_out, m3_out, m5_out, m7_out, m11_out,
       m13_out, not_1_out, not_2_out, not_3_out, not_4_out;

  not not_1 (not_1_out, A);
  not not_2 (not_2_out, B);
  not not_3 (not_3_out, C);
  not not_4 (not_4_out, D);
  and m2 (m2_out, not_1_out, not_2_out, C, not_4_out);
  and m3 (m3_out, not_1_out, not_2_out, C, D);
  and m5 (m5_out, not_1_out, B, not_3_out, D);
  and m7 (m7_out, not_1_out, B, C, D);
  and m11 (m11_out, A, not_2_out, C, D);
  and m13 (m13_out, A, B, not_3_out, D);
  and A_prime_B_prime_C (A_prime_B_prime_C_out, not_1_out, not_2_out, C);
  and B_prime_CD (B_prime_CD_out, not_2_out, C, D);
  and A_prime_BD (A_prime_BD_out, not_1_out, B, D);
  and BC_prime_D (BC_prime_D_out, B, not_3_out, D);
  or C_D (C_D_out, C, D);
  or B_C (B_C_out, B, C);
  or A_prime_D (A_prime_D_out, not_1_out, D);
  or B_prime_D (B_prime_D_out, not_2_out, D);
  or A_prime_B_prime_C_prime (A_prime_B_prime_C_prime_out, not_1_out, not_2_out, not_3_out);
  or SoP (F_can, m2_out, m3_out, m5_out, m7_out, m11_out, m13_out);
  or SoP_2 (F_sop, A_prime_B_prime_C_out, B_prime_CD_out, A_prime_BD_out, BC_prime_D_out);
  and PoS (F_pos, C_D_out, B_C_out, A_prime_D_out, B_prime_D_out, A_prime_B_prime_C_prime_out);
  xnor xnor_1 (EQ1, F_can, F_sop);
  xnor xnor_2 (EQ2, F_can, F_pos);
endmodule

module THINGHIEM5 (
  input  A,
  input  B,
  input  C,
  output out_4
);

  wire xor_1_out;

  xor xor_1 (xor_1_out, A, B);
  xor xor_2 (out_4, xor_1_out, C);
endmodule
